# Fritzing sketch OneMotorfzz (saved by Fritzing 0.9.2b)
breadboards: 1

parts:
  Part1 = Arduino Nano (Rev3.0)
  IC1 = L293D [package=THT]
  M1 = DC Motor
  VCC1 = Battery
  Part3 = Bluetooth Mate Silver  # not connected

nets:
  N1: Part1.GND, IC1.0V, VCC1.-
  N2: Part1.D3, IC1.In_3
  N3: Part1.D4, IC1.In_4
  N4: Part1.5V, IC1.Enable_1, IC1.+V
  N5: IC1.Enable_2, VCC1.+
  N6: IC1.Out_3_(_Controlled_by_Enable_2_), M1.pin_2
  N7: IC1.Out_4_(_Controlled_by_Enable_2_), M1.pin_1

notes:
  HC-05 (or HC-06)
  RXD TXD GND VCC
