# Fritzing sketch TwoMotor (saved by Fritzing 0.9.2b)
breadboards: 1

parts:
  Part2 = Arduino Nano (Rev3.0)
  IC2 = L293D [package=THT]
  M2 = DC Motor
  VCC2 = Battery
  M3 = DC Motor

nets:
  N1: Part2.GND, IC2.0V, VCC2.-
  N2: Part2.D3, IC2.In_3
  N3: Part2.D4, IC2.In_4
  N4: Part2.D8, IC2.In_2
  N5: Part2.D9, IC2.In_1
  N6: Part2.5V, IC2.Enable_1, IC2.+V
  N7: IC2.Out_1_(_Controlled_by_Enable_1_), M3.pin_2
  N8: IC2.Out_2_(_Controlled_by_Enable_1_), M3.pin_1
  N9: IC2.+Vmotor, IC2.Enable_2, VCC2.+
  N10: IC2.Out_3_(_Controlled_by_Enable_2_), M2.pin_2
  N11: IC2.Out_4_(_Controlled_by_Enable_2_), M2.pin_1

notes:
  HC-05 (or HC-06)
  RXD TXD GND VCC
